# Fritzing sketch MojitoBot (saved by Fritzing 0.9.3b)
breadboards: 1

parts:
  パーツ1 = Arduino Mega 2560 (Rev3)
  J1 = Piezo Speaker
  M1 = DC Motor
  KY-1 = Keyes Relay [package=THT]
  S3 = Pushbutton [package="[THT]"]
  S4 = Pushbutton [package="[THT]"]
  S5 = Pushbutton [package="[THT]"]
  Power_plug1 = Power plug
  DOTSTAR2 = DotStar Strip -- White (60/m) [part_number=2240]
  パーツ2 = NeoPixel Stick [part_number=1426]
  BUTTON1 = Arcade Button (green)
  NEOPIXEL1 = Neopixel Strip -- White (30/m) [part_number=1376]
  OLED_I2C1 = OLED 128x64 I2C Monochrome Display
  U1 = L9110 H-bridge module [part_number="L9110 H-bridge"]
  Power_plug2 = Power plug
  パーツ3 = NeoPixel Stick [part_number=1426]
  BUTTON2 = Arcade Button (white)

nets:
  N1: パーツ1.A0, U1.A-IB
  N2: パーツ1.A1, U1.A-IA
  N3: パーツ1.D21/SCL, OLED_I2C1.SCK
  N4: パーツ1.D20/SDA, OLED_I2C1.SDA
  GND: パーツ1.GND, J1.pin1, KY-1.ground, S3.Pin_3, S3.Pin_4, S4.Pin_3, S4.Pin_4, S5.Pin_3, S5.Pin_4, Power_plug1.GND, DOTSTAR2.GND, パーツ2.GND, BUTTON1.no_name_yet#2, NEOPIXEL1.GND, OLED_I2C1.GND, パーツ3.GND, BUTTON2.no_name_yet#2
  N5: パーツ1.D13_PWM, S5.Pin_1, S5.Pin_2
  N6: パーツ1.D12_PWM, S4.Pin_1, S4.Pin_2
  N7: パーツ1.D11_PWM, S3.Pin_1, S3.Pin_2
  N8: パーツ1.D10_PWM, パーツ2.DATAIN
  N9: パーツ1.D9_PWM, パーツ3.DATAIN
  N10: パーツ1.D8_PWM, DOTSTAR2.DI
  +5V: パーツ1.5V, KY-1.power, Power_plug1.VCC, DOTSTAR2.+5V, パーツ2.+5V, NEOPIXEL1.+5V, OLED_I2C1.VDD, パーツ3.+5V
  N11: パーツ1.D2_PWM, BUTTON2.no_name_yet#1
  N12: パーツ1.D3_PWM, BUTTON1.no_name_yet#1
  N13: パーツ1.D5_PWM, NEOPIXEL1.Din
  N14: パーツ1.D6_PWM, J1.pin2
  N15: パーツ1.D7_PWM, KY-1.signal
  N16: M1.pin_1, U1.MOTOR_A-B
  N17: M1.pin_2, U1.MOTOR_A-A
  GND_2: U1.GND, Power_plug2.GND
  VCC: U1.VCC, Power_plug2.VCC

notes:
  ラム出し機
  ソーダ用エアーポンプ
  モーター調整、ソーダ追加
  ソーダの水位計
  A8〜A14
  S ingle/Double表示
  5V
  ラムタワー装飾用
  Select
  Start
  パネル用
  ソーダ用

custom parts:
  Keyes Relay: The Keyes 5V relay module is suitable for SCM development, home appliance control. It uses a 5V~12V TIL control signal which can control DC / AC signal.
  DotStar Strip -- White (60/m): NeopixelDotStar Strip, White, 60 pixels per meter.
  NeoPixel Stick: Make your own little LED strip arrangement with this stick of NeoPixel LEDs. We crammed 8 of the tiny 5050 (5mm x 5mm) smart RGB LEDs onto a PCB with mounting holes and a chainable design. Use only one microcontroller pin to control as many as you can chain together! Each LED is addressable as the driver chip is inside the LED. Each one has ~18mA constant current drive so the color will be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
  Arcade Button (green): Adafruit Arcade Button (green)
  Neopixel Strip -- White (30/m): These NeoPixel strips have 30 digitally-addressable pixel LEDs per meter and are very affordable and are only 12.5 mm wide, 10 mm if you remove the strip from the casing.
  Arcade Button (white): Adafruit Arcade Button (white)
